# Fritzing sketch pcb_io_2015 (saved by Fritzing 0.9.1b)
circuit board: 7cm x 4cm
breadboards: 3

parts:
  5VData = female pin header, 2 pins [form="♀ (female)"]
  J1 = female pin header, 19 pins [form="♀ (female)"]
  J2 = female pin header, 19 pins [form="♀ (female)"]
  J4 = female pin header, 19 pins [form="♀ (female)"]
  J6 = female pin header, 19 pins [form="♀ (female)"]
  J8 = female pin header, 19 pins [form="♀ (female)"]
  C2 = Ceramic Capacitor [capacitance=100nF package="100 mil [THT, multilayer]"]
  C3 = Ceramic Capacitor [capacitance=100nF package="100 mil [THT, multilayer]"]
  C4 = Ceramic Capacitor [capacitance=100nF package="100 mil [THT, multilayer]"]
  PWR = LED - 5mm [color="Red (633nm)" package="5 mm [THT]"]
  C5 = Electrolytic Capacitor [capacitance=100nF package="100 mil [THT, electrolytic]"]
  C6 = Electrolytic Capacitor [capacitance=1µF package="100 mil [THT, electrolytic]"]
  J5 = female pin header, 10 pins [form="♀ (female)"]
  J9 = female pin header, 9 pins [form="♀ (female)"]
  5VPwr = female pin header, 2 pins [form="♀ (female)"]
  C7 = Ceramic Capacitor [capacitance=100nF package="100 mil [THT, multilayer]"]
  C8 = Ceramic Capacitor [capacitance=100nF package="100 mil [THT, multilayer]"]
  Teensy++2 = Teensy++ 2.0
  PA7-35 = female pin header, 3 pins [form="♀ (female)"]
  PA3-31 = female pin header, 3 pins [form="♀ (female)"]

nets:
  N1: 5VData.pin1, J4.pin1, J4.pin2, J4.pin3, J4.pin4, J4.pin5, J4.pin6, J4.pin7, J4.pin8, J4.pin9, J4.pin10, J4.pin11, J4.pin12, J4.pin13, J4.pin14, J4.pin15, J4.pin16, J4.pin17, J4.pin18, J4.pin19, J6.pin1, J6.pin2, J6.pin3, J6.pin4, J6.pin5, J6.pin6, J6.pin7, J6.pin8, J6.pin9, J6.pin10, J6.pin11, J6.pin12, J6.pin13, J6.pin14, J6.pin15, J6.pin16, J6.pin17, J6.pin18, J6.pin19, C2.1, C3.1, C4.1, PWR.cathode, C5.-, C6.-, 5VPwr.pin1, C7.0, C8.0, Teensy++2.GND#0, Teensy++2.GND#21, PA7-35.pin1, PA3-31.pin1
  N2: 5VData.pin2, J8.pin1, J8.pin2, J8.pin3, J8.pin4, J8.pin5, J8.pin6, J8.pin7, J8.pin8, J8.pin9, J8.pin10, J8.pin11, J8.pin12, J8.pin13, J8.pin14, J8.pin15, J8.pin16, J8.pin17, J8.pin18, J8.pin19, PWR.anode, C6.+, J9.pin1, J9.pin2, J9.pin3, J9.pin4, J9.pin5, J9.pin6, J9.pin7, J9.pin8, J9.pin9, Teensy++2.VCC, PA7-35.pin2, PA3-31.pin2
  N3: J1.pin1, C8.1, Teensy++2.B6
  N4: J1.pin2, C7.1, Teensy++2.B5
  N5: J1.pin3, Teensy++2.B4
  N6: J1.pin4, Teensy++2.B3
  N7: J1.pin5, Teensy++2.B2
  N8: J1.pin6, Teensy++2.B1
  N9: J1.pin7, Teensy++2.B0
  N10: J1.pin8, Teensy++2.E7
  N11: J1.pin9, Teensy++2.E6
  N12: J1.pin10, Teensy++2.GND#32
  N13: J1.pin11, Teensy++2.AREF
  N14: J1.pin12, Teensy++2.F0
  N15: J1.pin13, Teensy++2.F1
  N16: J1.pin14, Teensy++2.F2
  N17: J1.pin15, Teensy++2.F3
  N18: J1.pin16, Teensy++2.F4
  N19: J1.pin17, C4.0, Teensy++2.F5
  N20: J1.pin18, C3.0, Teensy++2.F6
  N21: J1.pin19, C2.0, Teensy++2.F7
  N22: J2.pin1, Teensy++2.B7
  N23: J2.pin2, Teensy++2.D0
  N24: J2.pin3, Teensy++2.D1
  N25: J2.pin4, Teensy++2.D2
  N26: J2.pin5, Teensy++2.D3
  N27: J2.pin6, Teensy++2.D4
  N28: J2.pin7, Teensy++2.D5
  N29: J2.pin8, Teensy++2.D6
  N30: J2.pin9, Teensy++2.D7
  N31: J2.pin10, Teensy++2.E0
  N32: J2.pin11, Teensy++2.E1
  N33: J2.pin12, Teensy++2.C0
  N34: J2.pin13, Teensy++2.C1
  N35: J2.pin14, Teensy++2.C2
  N36: J2.pin15, Teensy++2.C3
  N37: J2.pin16, Teensy++2.C4
  N38: J2.pin17, Teensy++2.C5
  N39: J2.pin18, Teensy++2.C6
  N40: J2.pin19, Teensy++2.C7
  N41: C5.+, J5.pin1, J5.pin2, J5.pin3, J5.pin4, J5.pin5, J5.pin6, J5.pin7, J5.pin8, J5.pin9, J5.pin10, 5VPwr.pin2
  N42: Teensy++2.PA3, PA3-31.pin3
  N43: Teensy++2.PA7, PA7-35.pin3

notes:
  VK
  Alim Power
  USB
  Alim Data

custom parts:
  Teensy++ 2.0: The Teensy is a complete USB-based microcontoller development system, in a very small footprint, capable of implementing many types of projects. All programming is done via the USB port. No special programmer is needed, only a standard "Mini-B" USB cable and a PC or Macintosh with a USB port.
